# Fritzing sketch AccessControl (saved by Fritzing 0.9.5d)
breadboards: 2

parts:
  R1 = Resistor [tolerance=±5% resistance=220 package=THT]
  R2 = Resistor [tolerance=±5% resistance=220 package=THT]  # not connected
  R3 = Resistor [tolerance=±5% resistance=220 package=THT]  # not connected
  LED1 = RGB LED (com. cathode, rbg) [package="5 mm [THT]"]
  J1 = Piezo Speaker  # not connected
  Part2 = RFID-RC522-v2
  Raspberry_Pi_1 = Raspberry Pi 3 [part_number=RPI-3-V1.2]
  J2 = T Cobbler Plus
  KY-1 = Keyes Relay [package=THT]
  S1 = Magnetic Door Switch [package=reed_switch_plastic]
  S2 = Momentary Switch [package=ksa_sealed_tac_switch]
  PIR1 = PIR sensor  # not connected

nets:
  N1: R1.Pin_1, LED1.green_anode
  N2: Part2.3.3V, S2.2, S2.4
  3V3: Raspberry_Pi_1.3v3, Raspberry_Pi_1.3V3, J2.3.3V
  N3: Raspberry_Pi_1.GPIO2, J2.GPIO_2
  N4: Raspberry_Pi_1.GPIO3, J2.GPIO_3
  N5: Raspberry_Pi_1.GIPO4, J2.GPIO_4
  GND: Raspberry_Pi_1.GND, J2.GND
  N6: Raspberry_Pi_1.GIPO17, J2.GPIO_17
  N7: Raspberry_Pi_1.GIPO27, J2.GPIO_27
  N8: Raspberry_Pi_1.GIPO22, J2.GPIO_22
  N9: Raspberry_Pi_1.GIPO10, J2.GPIO_10
  N10: Raspberry_Pi_1.GIPO9, J2.GPIO_9
  N11: Raspberry_Pi_1.GIPO11, J2.GPIO_11
  N12: Raspberry_Pi_1.ID_SD, J2.ID_SD
  N13: Raspberry_Pi_1.GIPO5, J2.GPIO_5
  N14: Raspberry_Pi_1.GIPO6, J2.GPIO_6
  N15: Raspberry_Pi_1.GIPO13, J2.GPIO_13
  N16: Raspberry_Pi_1.GIPO19, J2.GPIO_19
  N17: Raspberry_Pi_1.GIPO26, J2.GPIO_26
  N18: Raspberry_Pi_1.GIPO21, J2.GPIO_21
  N19: Raspberry_Pi_1.GIPO20, J2.GPIO_20
  N20: Raspberry_Pi_1.GIPO16, J2.GPIO_16
  N21: Raspberry_Pi_1.GIPO12, J2.GPIO_12
  N22: Raspberry_Pi_1.ID_SC, J2.ID_SC
  N23: Raspberry_Pi_1.GIPO7, J2.GPIO_7
  N24: Raspberry_Pi_1.GIPO8, J2.GPIO_8
  N25: Raspberry_Pi_1.GIPO25, J2.GPIO_25
  N26: Raspberry_Pi_1.GIPO24, J2.GPIO_24
  N27: Raspberry_Pi_1.GIPO23, J2.GPIO_23
  N28: Raspberry_Pi_1.GIPO18, J2.GPIO_18
  N29: Raspberry_Pi_1.GIPO15, J2.GPIO_15
  N30: Raspberry_Pi_1.GIPO14, J2.GPIO_14
  5V: Raspberry_Pi_1.5V, J2.5V
  N31: KY-1.power, S1.1
  N32: S2.1, S2.3

custom parts:
  RFID-RC522-v2: A simple China made RFID-RC522 Reader; do check the pin labels, as this is a MFRC522 based clone.
  T Cobbler Plus: The T-Cobbler Plus is an add on prototyping board from Adafruit specifically designed for the Raspberry Pi B+ that can break out all those tasty power, GPIO, I2C and SPI pins from the 40-pin header onto a solderless breadboard. This set will make "cobbling together" prototypes with the Pi super easy. The T-Cobbler Plus can plug into any solderless breadboard.
  Keyes Relay: The Keyes 5V relay module is suitable for SCM development, home appliance control. It uses a 5V~12V TIL control signal which can control DC / AC signal.
